# Fritzing sketch draft (saved by Fritzing 0.8.7b)

parts:
  Componente1 = Arduino Uno (Rev3)  # not connected
  Componente2 = Arduino Prototyping Shield
  RF_Receiver1 = RF_Receiver
  RF_Sender_433_Mhz1 = RF Sender
  LED1 = LED - 5mm [color="Red (633nm)" package="5 mm [THT]"]
  LED3 = LED - 5mm [color="Yellow (595nm)" package="5 mm [THT]"]
  LED4 = LED - 5mm [color="Infrared (940nm)" package="5 mm [THT]"]
  LED5 = LED - 5mm [color="Infrared (940nm)" package="5 mm [THT]"]
  LED2 = LED - 5mm [color="Green (555nm)" package="5 mm [THT]"]
  R1 = Resistor [tolerance=±5% resistance=82 package=THT]
  NPN_Transistor1 = NPN-Transistor [package="TO92 [THT]"]
  IR1 = TSOP312.., 314.. [package=THT]
  R3 = Resistor [tolerance=±5% resistance=82 package=THT]
  R4 = Resistor [tolerance=±5% resistance=33k package=THT]
  R5 = Resistor [tolerance=±5% resistance=82 package=THT]
  R6 = Resistor [tolerance=±5% resistance=270 package=THT]
  Componente3 = Arduino Prototyping Shield
  R7 = Resistor [tolerance=±5% resistance=82 package=THT]
  R8 = Resistor [tolerance=±5% resistance=82 package=THT]
  R9 = Resistor [tolerance=±5% resistance=33k package=THT]
  R10 = Resistor [tolerance=±5% resistance=82 package=THT]
  NPN_Transistor2 = NPN-Transistor [package="TO92 [THT]"]
  R11 = Resistor [tolerance=±5% resistance=270 package=THT]
  RF_Receiver2 = RF_Receiver
  LED6 = LED - 5mm [color="Yellow (595nm)" package="5 mm [THT]"]
  LED7 = LED - 5mm [color="Red (633nm)" package="5 mm [THT]"]
  LED8 = LED - 5mm [color="Green (555nm)" package="5 mm [THT]"]
  LED9 = LED - 5mm [color="Infrared (940nm)" package="5 mm [THT]"]
  LED10 = LED - 5mm [color="Infrared (940nm)" package="5 mm [THT]"]
  IR2 = TSOP312.., 314.. [package=THT]

nets:
  GND: Componente2.GND, Componente2.N$203, Componente2.N$235, Componente2.N$362, Componente2.N$367, Componente2.N$371, RF_Receiver1.GND, LED1.cathode, LED3.cathode, LED2.cathode, NPN_Transistor1.E, IR1.GND
  N1: Componente2.D8, Componente2.N$411, R5.Pin_1
  N2: Componente2.D9, Componente2.N$310, R4.Pin_1
  N3: Componente2.D1(TX), IR1.Data
  N4: Componente2.D2, RF_Receiver1.DIN
  N5: Componente2.D3, Componente2.N$38, R3.Pin_1
  N6: Componente2.D5, Componente2.N$305
  N7: Componente2.D7, Componente2.N$413, R1.Pin_1
  +5V: Componente2.+5V, Componente2.N$48, Componente2.N$281, Componente2.N$315, Componente2.N$360, RF_Receiver1.VIN, IR1.Vs
  N8: Componente2.+9V, Componente2.N$356, R6.Pin_1
  N9: Componente2.N$369, LED4.cathode, LED5.cathode, NPN_Transistor1.C
  N10: Componente2.N$370, Componente2.N$379, NPN_Transistor1.B, R3.Pin_0
  N11: Componente2.N$399, LED2.anode, R4.Pin_0
  N12: Componente2.N$402, LED1.anode, R5.Pin_0
  N13: Componente2.N$405, LED3.anode
  N14: Componente2.N$406, R1.Pin_0
  GND_2: RF_Sender_433_Mhz1.GND, Componente3.N$191, Componente3.N$235, RF_Receiver2.GND
  N15: RF_Sender_433_Mhz1.DIN, Componente3.D5, Componente3.N$16
  VIN: RF_Sender_433_Mhz1.VIN, Componente3.+5V, Componente3.N$276, Componente3.N$314, Componente3.N$360, RF_Receiver2.VIN, IR2.Vs
  N16: LED4.anode, LED5.anode, R6.Pin_0
  N17: Componente3.D12, Componente3.D0(RX), IR2.Data
  N18: Componente3.D13, Componente3.N$405, R10.Pin_0, LED6.anode
  GND_3: Componente3.GND, Componente3.D2, Componente3.N$247, NPN_Transistor2.E, RF_Receiver2.DIN, LED6.cathode, LED7.cathode, LED8.cathode, IR2.GND
  N19: Componente3.D1(TX), R10.Pin_1
  N20: Componente3.D3, Componente3.N$429, R7.Pin_1
  N21: Componente3.D4, Componente3.N$400, R8.Pin_1
  N22: Componente3.D6, Componente3.N$413, R9.Pin_1
  N23: Componente3.+9V, Componente3.N$365, R11.Pin_1
  N24: Componente3.N$17, R8.Pin_0, LED7.anode
  N25: Componente3.N$227, Componente3.N$433, R7.Pin_0, NPN_Transistor2.B
  N26: Componente3.N$229, NPN_Transistor2.C, LED9.cathode, LED10.cathode
  N27: Componente3.N$325, Componente3.N$327, R11.Pin_0, LED9.anode, LED10.anode
  N28: Componente3.N$406, R9.Pin_0, LED8.anode

custom parts:
  TSOP312.., 314..: The TSOP312.., TSOP314.. series are miniaturized receivers for infrared remote control systems. A PIN diode and a preamplifier are assembled on a lead frame, the epoxy package acts as an IR filter. The demodulated output signal can be directly decoded by a microprocessor. The TSOP312.. is compatible with all common IR remote control data formats. The TSOP314.. is optimized to suppress almost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
